# Fritzing sketch esp12-e_with_soil-moisture-sensor (saved by Fritzing 0.9.6b)

parts:
  U1 = ESP-12F [part_number=ESP-12F]
  U2 = Voltage Regulator -- 3.3 V -- LM1117
  U3 = LIPO-1000mAh [package=lipo-1000]
  C1 = Electrolytic Capacitor [capacitance=100µF voltage=35V package="200 mil [THT, electrolytic]"]
  M2 = MT3608 Module
  Capacitive_Soil_Moisture_Sensor2 = DFRobot Capacitive Soil Moisture Sensor V1.0 [part_number=SEN0193]
  R1 = Resistor [tolerance=±5% resistance=220 package="0805 [SMD]"]
  R2 = Resistor [tolerance=±5% resistance=220 package="0402 [SMD]"]
  TP1 = TP4056 [chip_label=TP4056 package="DIP (Dual Inline) [THT]"]
  C2 = Capacitor [package=cap-pth-small2]

nets:
  N1: U1.pad2, R1.Pin_0, R2.Pin_0
  N2: U1.pad3, U2.IN
  N3: U1.pad16, U2.GND, C1.-, TP1.pin6, C2.2
  N4: U2.OUT, TP1.pin3
  N5: U3.+, TP1.pin4
  N6: U3.-, TP1.pin5
  N7: C1.+, C2.1
  N8: M2.pin3, Capacitive_Soil_Moisture_Sensor2.VCC
  N9: M2.pin4, Capacitive_Soil_Moisture_Sensor2.GND
  N10: Capacitive_Soil_Moisture_Sensor2.A, R1.Pin_1

notes:
  MCP1700-3302E/TO-92 LDO
  22K
  15K
  100nF
  100nF (optional)

custom parts:
  ESP-12F: <>The ESP-12F is a processor module, originally produced by AI-Thinker, with built-in WiFI capabilities and based on the ESP8266 MCU produced by Espressif Systems. Links: Product Specification Espressif Systems ESP8266 MCU
  Voltage Regulator -- 3.3 V -- LM1117: LM1117-3.3 Voltage regulator, 3.3 V output. Note that the pinout order is not the same as LM7805 or LM7833.
  MT3608 Module: MT3608 Boost Converter Module Links: Aerosemi MT3608 2A Step Up Converter datasheet
  DFRobot Capacitive Soil Moisture Sensor V1.0: DFRobot Capacitive Soil Moisture Sensor V1.0 This product measures soil moisture levels by capacitive sensing, rather than resistive sensing like other types of moisture sensor. It is made of a corrosion resistant material giving it a long service life. Insert it into soil and impress your friends with the real-time soil moisture data! The product includes an on-board voltage regulator which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
  TP4056: A DIP stand-in part for whatever IC you want. With 6 pins on a 300mil dual inline package (DIP) footprint.
