# Fritzing sketch wireing-issue (saved by Fritzing 0.9.6b)

parts:
  R1 = Resistor [tolerance=±0.1% resistance=150k package="2010 [SMD]"]
  R2 = Resistor [tolerance=±0.1% resistance=39 package="2010 [SMD]"]
  Capacitive_Soil_Moisture_Sensor1 = DFRobot Capacitive Soil Moisture Sensor V1.0 [part_number=SEN0193]
  M1 = MT3608 Module
  U1 = NodeMCU V3.0

nets:
  N1: R1.Pin_0, Capacitive_Soil_Moisture_Sensor1.A
  N2: R1.Pin_1, R2.Pin_0, U1.A0
  N3: R2.Pin_1, M1.pin1, U1.GND
  N4: Capacitive_Soil_Moisture_Sensor1.VCC, M1.pin3
  N5: Capacitive_Soil_Moisture_Sensor1.GND, M1.pin4
  N6: M1.pin2, U1.3V3

notes:
  R1=150 Ohm
  R2=39 Ohm
  5.5V
  Output - Wet = 2,34V
  Output - Dry = 4.54V
  Dry = 8,3mv
  Wet = 7,7mV

custom parts:
  DFRobot Capacitive Soil Moisture Sensor V1.0: DFRobot Capacitive Soil Moisture Sensor V1.0 This product measures soil moisture levels by capacitive sensing, rather than resistive sensing like other types of moisture sensor. It is made of a corrosion resistant material giving it a long service life. Insert it into soil and impress your friends with the real-time soil moisture data! The product includes an on-board voltage regulator which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
  MT3608 Module: MT3608 Boost Converter Module Links: Aerosemi MT3608 2A Step Up Converter datasheet
  NodeMCU V3.0: ESP8266 based NodeMCU
